# Fritzing sketch Arduino L298N (saved by Fritzing 0.9.2b)

parts:
  S1 = H-Bridge with L298N
  Parte1 = Arduino Uno (Rev3)
  VCC1 = 4 x AAA Battery Mount
  U1 = SWITCH-SPST-2 [package=switch-spst-vertical]
  M1 = DC Motor
  M2 = DC Motor

nets:
  N1: S1.12V, U1.P
  GND: S1.GND, Parte1.GND, VCC1.-
  5V: S1.5V, Parte1.VIN
  N2: S1.ENA, Parte1.D6_PWM
  N3: S1.IN1, Parte1.D13/SCK
  N4: S1.IN2, Parte1.D12/MISO
  N5: S1.IN3, Parte1.D11_PWM/MOSI
  N6: S1.IN4, Parte1.D10_PWM/SS
  N7: S1.ENB, Parte1.D5_PWM
  N8: S1.M1-01, M1.pin_2
  N9: S1.M1-02, M1.pin_1
  N10: S1.M2-01, M2.pin_2
  N11: S1.M2-02, M2.pin_1
  N12: VCC1.+, U1.O

custom parts:
  H-Bridge with L298N: h-bridge
